// Logisim project full adder.circ as structural Verilog: 1 circuit, main circuit main
module main (
  input  A,
  input  B,
  input  C,
  output S,
  output C_2
);

  wire AND_2_out, AND_out, XOR_out;

  xor XOR (XOR_out, A, B);
  xor XOR_2 (S, XOR_out, C);
  and AND (AND_out, C, XOR_out);
  and AND_2 (AND_2_out, B, A);
  or OR (C_2, AND_out, AND_2_out);
endmodule
