// Logisim project full subtractor.circ as structural Verilog: 1 circuit, main circuit main
module main (
  input  A,
  input  B,
  input  B_in,
  output D,
  output B_out
);

  wire and_1_out, and_2_out, not_1_out, not_2_out, xor_1_out;

  xor xor_1 (xor_1_out, A, B);
  not not_1 (not_1_out, A);
  not not_2 (not_2_out, xor_1_out);
  xor xor_2 (D, xor_1_out, B_in);
  and and_1 (and_1_out, not_2_out, B_in);
  and and_2 (and_2_out, not_1_out, B);
  or or_1 (B_out, and_1_out, and_2_out);
endmodule
